// Logisim project priority encoder.circ as structural Verilog: 1 circuit, main circuit Encoder_4to2
module Encoder_4to2 (
);

  wire and_1_out, and_2_out, and_3_out, and_4_out, and_5_out, and_6_out, D0_sw1, D1_sw1, D2_sw1, D3_sw1,
       D4_sw1, D5_sw1, D6_sw1, D7_sw1, not_1_out, not_2_out, not_3_out, not_4_out, or_1_out, or_2_out,
       or_3_out, or_4_out, or_5_out, or_6_out, or_7_out, or_8_out, or_9_out;

  DipSwitch #(.number(1)) D3 (.sw1(D3_sw1));
  DipSwitch #(.number(1)) D2 (.sw1(D2_sw1));
  DipSwitch #(.number(1)) D1 (.sw1(D1_sw1));
  DipSwitch #(.number(1)) D0 (.sw1(D0_sw1));
  DipSwitch #(.number(1)) D7 (.sw1(D7_sw1));
  DipSwitch #(.number(1)) D6 (.sw1(D6_sw1));
  DipSwitch #(.number(1)) D5 (.sw1(D5_sw1));
  DipSwitch #(.number(1)) D4 (.sw1(D4_sw1));
  not not_1 (not_1_out, D2_sw1);
  not not_2 (not_2_out, D6_sw1);
  and and_1 (and_1_out, not_1_out, D1_sw1);
  or or_1 (or_1_out, D3_sw1, D2_sw1);
  and and_2 (and_2_out, not_2_out, D5_sw1);
  or or_2 (or_2_out, D7_sw1, D6_sw1);
  or or_3 (or_3_out, or_1_out, D1_sw1, D0_sw1);
  or or_4 (or_4_out, D7_sw1, and_2_out);
  or or_5 (or_5_out, or_2_out, D5_sw1, D4_sw1);
  or or_6 (or_6_out, D3_sw1, and_1_out);
  not not_3 (not_3_out, or_5_out);
  and and_3 (and_3_out, or_6_out, not_3_out);
  and and_4 (and_4_out, or_4_out, or_5_out);
  and and_5 (and_5_out, or_1_out, not_3_out);
  and and_6 (and_6_out, or_2_out, or_5_out);
  or or_7 (or_7_out, and_3_out, and_4_out);
  or or_8 (or_8_out, and_5_out, and_6_out);
  or or_9 (or_9_out, or_3_out, or_5_out);
  not not_4 (not_4_out, or_9_out);
  LED C (.in(or_7_out));
  LED B (.in(or_8_out));
  LED A (.in(or_5_out));
  LED NI (.in(not_4_out));
endmodule
